# Fritzing sketch rasp (saved by Fritzing 0.9.4)
breadboards: 1

parts:
  Mod1 = Raspberry Pi Pico
  J1 = Piezo Speaker
  LED2 = LED - 5mm [color="Red (633nm)" package="5 mm [THT]"]
  R1 = Resistor [tolerance=±5% resistance=220 package=THT]
  R2 = Resistor [tolerance=±5% resistance=220 package=THT]
  Matrix_keypad1 = KEYPAD 4x4
  Display1 = LCD screen 16x2 IIC [part_number=101290]
  KY-1 = Keyes Relay [package=THT]
  LED3 = LEDs [package=led10mm]

nets:
  N1: Mod1.pin_1, Display1.SDA
  N2: Mod1.pin_2, Display1.SCL
  N3: Mod1.pin_3, Mod1.pin_8, Mod1.pin_13, Mod1.pin_18, Mod1.pin_23, Mod1.pin_28, Mod1.pin_33, Mod1.pin_38, Mod1.pin_42, J1.pin1, R2.Pin_1, KY-1.ground
  N4: Mod1.pin_4, J1.pin2, LED2.anode
  N5: Mod1.pin_5, LED3.A
  N6: Mod1.pin_6, KY-1.signal
  N7: Mod1.pin_26, Matrix_keypad1.row1
  N8: Mod1.pin_27, Matrix_keypad1.row2
  N9: Mod1.pin_29, Matrix_keypad1.row3
  N10: Mod1.pin_31, Matrix_keypad1.row4
  N11: Mod1.pin_36, R1.Pin_1, KY-1.power

custom parts:
  Raspberry Pi Pico: Raspberry Pi Pico. Based around the RP2040 microcontroller the Pico is a low cost microcontroller device bringing Raspberry Pi quality, cost, and easy of use to the microcontroller space. Jan 2021, Split part in to two versions: tht (this one) and SMD. This one will drill holes for a .1 in header in pcb to allow plugging in the module as well as providing pads to solder the module to the top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
  KEYPAD 4x4: Matrix keypad 16 buttons, 4 rows x 4 columns
  LCD screen 16x2 IIC: LCD screen with HD44780 controller enables showing text, symbols, value or anything else that comes from Croduino/Arduino. It is capable of showing 16 symbols in two lines and therefore can be used in many projects that need to send clearly visible and legible output information.. • Color of symbols: White • Backlight: Blue • Dimensions: 80 x 36 x 12 mm • Screen dimensions: 64.5 x 16 mm •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
  Keyes Relay: The Keyes 5V relay module is suitable for SCM development, home appliance control. It uses a 5V~12V TIL control signal which can control DC / AC signal.

// code stored in the sketch: ex.ino
# BARCODE
#systeme code & diagram
import machine
from machine import Pin , I2C
from lcd_api import LcdApi
from pico_i2c_lcd import I2cLcd
import time
import utime
ledrouge = Pin(2,Pin.OUT)
ledvert = Pin(3,Pin.OUT)
relais = Pin(12,Pin.OUT)
addressi2c = 0x27
rows = 2
columns = 16
i2c = I2C(0,sda=machine.Pin(0),scl= machine.Pin(1),freq= 400000)
lcd = I2cLcd(i2c, addressi2c,rows,columns)
matrix_keys = [['1', '2', '3', 'A'],
               ['4', '5', '6', 'B'],
               ['7', '8', '9', 'C'],
               ['*', '0', '#', 'D']]
keypad_rows = [16,17,18,19]
keypad_columns = [20,21,22,26]
col_pins = []
row_pins = []
secret_pin = ['2','2','3','4','5','5']
guess = []
for x in range(0,4):
    row_pins.append(Pin(keypad_rows[x], Pin.OUT))
    row_pins[x].value(1)
    col_pins.append(Pin(keypad_columns[x], Pin.IN, Pin.PULL_DOWN))
    col_pins[x].value(0)
    
    
print("Please enter a key from the keypad")
    
def scankeys():
    lcd.move_to(0,0)
    lcd.putstr("password :" )
    for row in range(4):
        for col in range(4):
            row_pins[row].high()
            key = None
            
            if col_pins[col].value() == 1:
                print("You have pressed:", matrix_keys[row][col])
                key_press = matrix_keys[row][col]
                utime.sleep(0.1)
                guess.append(key_press)
            for i in range(len(guess)):
                lcd.move_to(i,1)
                lcd.putstr(guess[i])
                
            if len(guess) == 6:
                checkPin(guess)
                
                for x in range(0,6):
                    guess.pop()
                    
                    
        row_pins[row].low()
def checkPin(guess):
             
    if guess == secret_pin:
        
        print("You got the secret pin correct")
        ledvert.value(1)
        utime.sleep(3)
        ledvert.value(0)
        lcd.move_to(1,0)
        lcd.putstr("correct")
        lcd.move_to(0,1)
        lcd.putstr("password")
        time.sleep(1)
        lcd.clear()
        
    else:
        print("Better luck next time")
        lcd.clear()
        lcd.move_to(1,0)
        lcd.putstr("incorrect")
        lcd.move_to(1,1)
        lcd.putstr("password")
        time.sleep(1)
        lcd.clear()
     
            


while True :
    scankeys()
    relais.value(1)
